# Fritzing sketch oef2 (saved by Fritzing 0.9.3b)
breadboards: 1

parts:
  Raspberry_Pi_1 = Raspberry Pi 3 [part_number=RPI-3-V1.2]
  LED1 = smd LED [color="Red (633nm)" package="0805 [SMD]"]
  LED2 = smd LED [color="Red (633nm)" package="0805 [SMD]"]
  R1 = Resistor [tolerance=±5% resistance=220 package="1206 [SMD]"]
  R2 = Resistor [tolerance=±5% resistance=220 package="1206 [SMD]"]
  S1 = SWITCH-MOMENTARY-2 [package=tactile-pth-12mm]
  S2 = SWITCH-MOMENTARY-2 [package=tactile-pth-12mm]
  S3 = SWITCH-MOMENTARY-2 [package=tactile-pth-12mm]

nets:
  N1: Raspberry_Pi_1.GPIO17, S1.1
  N2: Raspberry_Pi_1.GPIO27, S2.1
  N3: Raspberry_Pi_1.GPIO22, S3.1
  N4: Raspberry_Pi_1.GPIO23, LED2.anode
  N5: Raspberry_Pi_1.GND, LED1.anode
  N6: Raspberry_Pi_1.GPIO18, R1.Pin_0, R2.Pin_0, S1.2, S2.2, S3.2
  N7: LED1.cathode, R1.Pin_1
  N8: LED2.cathode, R2.Pin_1
